# Fritzing sketch Cadiofréquencemètre (saved by Fritzing 0.9.3b)
breadboards: 1

parts:
  Q1 = LTR-301 [package=ltr-301]
  R5 = Resistor [tolerance=±5% resistance=220 package=THT]
  R2 = Resistor [tolerance=±5% resistance=220 package=THT]
  Part1 = Arduino Uno (Rev3)
  LED1 = LED - 5mm [color="Infrared (940nm)" package="5 mm [THT]"]
  R1 = Resistor [tolerance=±5% resistance=2.2k package=THT]
  R3 = Resistor [tolerance=±5% resistance=68k package=THT]
  IC1 = LM324 [package=dil16]
  C2 = Ceramic Capacitor [capacitance=100nF package="100 mil [THT, multilayer]"]
  C1 = Ceramic Capacitor [capacitance=1µF package="100 mil [THT, multilayer]"]
  R6 = Resistor [tolerance=±5% resistance=220 package=THT]
  R4 = Resistor [tolerance=±5% resistance=220 package=THT]
  LED2 = LED - 5mm [color="Red (633nm)" package="5 mm [THT]"]

nets (from the schematic view):
  N1: Q1.C, R2.Pin_1, C1.1
  GND: Q1.E, Part1.GND, LED1.cathode, R3.Pin_0, IC1.GND, R4.Pin_1, LED2.cathode
  N2: R5.Pin_0, IC1.OUT2, C2.0, R6.Pin_0
  N3: R5.Pin_1, IC1.IN2-, C2.1, R4.Pin_0
  N4: R2.Pin_0, Part1.5V, R1.Pin_1, IC1.V+
  N5: Part1.A0, R6.Pin_1, LED2.anode
  N6: LED1.anode, R1.Pin_0
  N7: R3.Pin_1, IC1.IN2+, C1.0

custom parts:
  LM324: LM324 Quad OpAmp

// code stored in the sketch: Untitled.ino

int valeur;

void setup() {
serial.begin = 9600;

valeur = analogRead(A0);
serial.print("valeur = ");
serial.println (valeur);

}


void loop (){

}
