# Fritzing sketch Coeur de LED (saved by Fritzing 0.9.3b)
breadboards: 1

parts:
  R1 = Resistor [tolerance=±5% resistance=220 package=THT]
  LED1 = LED - 5mm [color="Red (633nm)" package="5 mm [THT]"]
  R2 = Resistor [tolerance=±5% resistance=220 package=THT]
  LED2 = LED - 5mm [color="Red (633nm)" package="5 mm [THT]"]
  R3 = Resistor [tolerance=±5% resistance=220 package=THT]
  LED3 = LED - 5mm [color="Red (633nm)" package="5 mm [THT]"]
  LED4 = LED - 5mm [color="Red (633nm)" package="5 mm [THT]"]
  R4 = Resistor [tolerance=±5% resistance=220 package=THT]
  R5 = Resistor [tolerance=±5% resistance=220 package=THT]
  LED5 = LED - 5mm [color="Red (633nm)" package="5 mm [THT]"]
  LED6 = LED - 5mm [color="Red (633nm)" package="5 mm [THT]"]
  R6 = Resistor [tolerance=±5% resistance=220 package=THT]
  LED7 = LED - 5mm [color="Red (633nm)" package="5 mm [THT]"]
  LED8 = LED - 5mm [color="Red (633nm)" package="5 mm [THT]"]
  R8 = Resistor [tolerance=±5% resistance=220 package=THT]
  R9 = Resistor [tolerance=±5% resistance=220 package=THT]
  LED9 = LED - 5mm [color="Red (633nm)" package="5 mm [THT]"]
  R10 = Resistor [tolerance=±5% resistance=220 package=THT]
  LED10 = LED - 5mm [color="Red (633nm)" package="5 mm [THT]"]
  R11 = Resistor [tolerance=±5% resistance=220 package=THT]
  Composant1 = Arduino Uno (Rev3)

nets:
  N1: R1.Pin_0, LED1.cathode
  N2: R1.Pin_1, R2.Pin_1, R3.Pin_1, R5.Pin_1, R6.Pin_1, R10.Pin_1, R11.Pin_1
  N3: LED1.anode, Composant1.D5_PWM
  N4: R2.Pin_0, LED2.cathode
  N5: LED2.anode, Composant1.D3_PWM
  N6: R3.Pin_0, LED3.cathode
  N7: LED3.anode, Composant1.D7
  N8: LED4.cathode, R4.Pin_1
  N9: LED4.anode, Composant1.D6_PWM
  N10: R4.Pin_0, R8.Pin_0
  N11: R5.Pin_0, LED5.cathode
  N12: LED5.anode, Composant1.D2
  N13: LED6.cathode, R9.Pin_1
  N14: LED6.anode, Composant1.D4
  N15: R6.Pin_0, LED7.cathode
  N16: LED7.anode, Composant1.D8
  N17: LED8.cathode, R8.Pin_1
  N18: LED8.anode, Composant1.D9_PWM
  N19: LED9.cathode, R10.Pin_0
  N20: LED9.anode, Composant1.D10_PWM/SS
  N21: LED10.cathode, R11.Pin_0
  N22: LED10.anode, Composant1.D1/TX
